# Fritzing sketch GGNES - pcbway build full (saved by Fritzing 0.9.3b)
circuit board: 3.62559cm x 4.94359cm
breadboards: 1

parts:
  J1 = female pin header, 2 pins [form="♀ (female)"]
  BLAST_PARSER_PROCESSOR = PIC24HJ32GP202 [part_number="28 pin dip socket" package=dil28-3]
  Pad8 = Pad [width=0.58437266405227717 height=0.44625078588235545 connect=center]
  Pad10 = Pad [width=0.6326495204626843 height=0.35179383829006988 connect=center]
  Pad11 = Pad [width=0.58437266405227717 height=0.44625078588235545 connect=center]
  Pad12 = Pad [width=0.58437266405227717 height=0.44625078588235545 connect=center]
  Pad14 = Pad [width=0.58437266405227717 height=0.44625078588235545 connect=center]
  J3 = female pin header, 14 pins [form="♀ (female)"]  # not connected
  J4 = female pin header, 14 pins [form="♀ (female)"]  # not connected
  J5 = female pin header, 2 pins [form="♀ (female)"]
  J6 = female pin header, 2 pins [form="♀ (female)"]
  J2 = female pin header, 10 pins [form="♀ (female)"]
  J2_2 = female pin header, 10 pins [form="♀ (female)"]
  J7 = male alternating pin header, 10 pins [form="♂ (male)" part_number="male header bent pin pointing over GGNES text"]

nets:
  N1: J1.pin1, BLAST_PARSER_PROCESSOR.AN1_VREF-_CN2_RA1
  N2: J1.pin2, BLAST_PARSER_PROCESSOR.AN0_VREF+_CN2_RA0
  N3: BLAST_PARSER_PROCESSOR.PGED1_AN2_C2IN-_RP0_CN4_RB0, J5.pin1
  N4: BLAST_PARSER_PROCESSOR.PGEC1_AN3_C2IN+_RP1_CN5_RB1, J5.pin2
  N5: BLAST_PARSER_PROCESSOR.AN4_RP2_CN6_RB2, J6.pin2
  N6: BLAST_PARSER_PROCESSOR.SOSCI_RP4_CN1_RB4, J2.pin6, J2_2.pin6, J7.pin6
  N7: BLAST_PARSER_PROCESSOR.PGEC3_ASCL1_RP6_CN24_RB6, J2.pin10, J2_2.pin10, J7.pin10
  N8: BLAST_PARSER_PROCESSOR.INT0_RP7_CN23_RB7, J2.pin9, J2_2.pin9, J7.pin9
  N9: BLAST_PARSER_PROCESSOR.TCK_SCL_RP8_CN22_RB8, J2.pin8, J2_2.pin8, J7.pin8
  N10: BLAST_PARSER_PROCESSOR.TDO_SDA1_RP9_CN12_RB9, J2.pin7, J2_2.pin7, J7.pin7
  N11: BLAST_PARSER_PROCESSOR.VSS, Pad11.pad
  N12: BLAST_PARSER_PROCESSOR.VCAP_VDDCORE, Pad8.pad, J6.pin1, J2.pin1, J2_2.pin1, J7.pin1
  N13: BLAST_PARSER_PROCESSOR.PGEC2_TMS_RP11_CN15_RB11, Pad14.pad, J2.pin2, J2_2.pin2, J7.pin2
  N14: BLAST_PARSER_PROCESSOR.AN12_RP12_CN14_RB12, J2.pin5, J2_2.pin5, J7.pin5
  N15: BLAST_PARSER_PROCESSOR.AN11_RP13_CN13_RB13, J2.pin4, J2_2.pin4, J7.pin4
  N16: BLAST_PARSER_PROCESSOR.AN10_RP14_CN12_RB14, J2.pin3, J2_2.pin3, J7.pin3
  N17: BLAST_PARSER_PROCESSOR.AN9_RP15_CN11_RB15, Pad10.pad
  N18: BLAST_PARSER_PROCESSOR.AVSS, Pad12.pad

notes:
  START
  1
  2
  RESET
  DOWN
  LEFT
  RIGHT
  UP
  GROUND
  5V
  Rx2
  GGNES
  RX1
  TX1
  TX2
  Disable
  v2  GameGearConsole.com
